# Fritzing sketch diagramme de circuit (saved by Fritzing 0.9.9b)
breadboards: 1

parts:
  U1 = RJ45 Jack [package=rj45-8]
  U2 = RJ45 Jack [package=rj45-8]
  ESP32 = Heltec WiFi LoRa 32 V2 [part_number=HTIT-WB32LA]

nets:
  N1: U1.1, ESP32.pin_23
  N2: U1.2, ESP32.pin_24
  N3: U1.3, ESP32.pin_25
  N4: U1.4, ESP32.pin_26
  N5: U1.5, ESP32.pin_27
  N6: U1.6, ESP32.pin_28
  N7: U1.7, ESP32.pin_29
  N8: U1.8, ESP32.pin_30
  N9: U2.1, ESP32.pin_14
  N10: U2.2, ESP32.pin_13
  N11: U2.3, ESP32.pin_12
  N12: U2.4, ESP32.pin_11
  N13: U2.5, ESP32.pin_10
  N14: U2.6, ESP32.pin_9
  N15: U2.7, ESP32.pin_8
  N16: U2.8, ESP32.pin_7
